# Fritzing sketch LED Simple_1-2 (saved by Fritzing 0.9.3b)
breadboards: 1

parts:
  U1 = NodeMCU V3.0
  R1 = Resistor [tolerance=±5% resistance=220 package="0805 [SMD]"]
  U2 = WS2812 RGB LED strip

nets:
  3V3: U1.3V3, U2.VCC
  N1: U1.GND#6, U1.GND#13, U1.GND#16, U1.GND#33, U2.GND
  N2: U1.RX, R1.Pin_1
  N3: R1.Pin_0, U2.DIN

custom parts:
  NodeMCU V3.0: ESP8266 based NodeMCU
  WS2812 RGB LED strip: WS2812 strip
