# Fritzing sketch Schaltung (saved by Fritzing 0.9.3b)
breadboards: 1

parts:
  U1 = NodeMCU V3.0
  U2 = WS2812 RGB LED strip
  R1 = Resistor [tolerance=±5% resistance=220 package=THT]
  HC-SR04_Sensor_1 = HC-SR04 Ultrasonic Distance Sensor

nets:
  GND: U1.GND#6, U1.GND#13, U1.GND#16, U1.GND#33, U2.GND, HC-SR04_Sensor_1.GND
  N1: U1.D7, HC-SR04_Sensor_1.ECHO
  N2: U1.D8, HC-SR04_Sensor_1.TRIG
  N3: U1.RX, R1.Pin_0
  VCC: U1.Vin, U2.VCC, HC-SR04_Sensor_1.VCC
  N4: U2.DIN, R1.Pin_1

custom parts:
  NodeMCU V3.0: ESP8266 based NodeMCU
  WS2812 RGB LED strip: WS2812 strip
